# Fritzing sketch acDimmer_new (saved by Fritzing 0.8.3b)
circuit board: 5.97605cm x 2.9069cm
breadboards: 1

parts:
  4n25 = Optocoupler [part_number=4N25 package=THT]
  J1 = screw terminal, 4 pins
  R1 = Resistor [tolerance=±5% resistance=33k package=THT]
  R2 = Resistor [tolerance=±5% resistance=470 package=THT]
  R3 = Resistor [tolerance=±5% resistance=10k package=THT]
  LED1 = LED - 5mm [color="Red (633nm)" package="5 mm [THT]"]
  R4 = Resistor [tolerance=±5% resistance=1k package=THT]
  R5 = Resistor [tolerance=±5% resistance=33k package=THT]
  Q1 = Basic FET N-Channel [part_number=TIC206 package="TO220 [THT]"]
  U5 = MOC3031-M [part_number=MOC3021 package=dil06]
  U4 = mystery part, 4 pins [chip_label=?]
  400V_Bridge = mystery part, 6 pins [chip_label=?]
  R6 = Resistor [tolerance=±5% resistance=1k package=THT]

nets:
  N1: 4n25.Pin_1, 400V_Bridge.pin1
  N2: 4n25.Pin_2, 400V_Bridge.pin2, 400V_Bridge.pin3
  N3: 4n25.Pin_4, U5.2, U4.pin4
  N4: 4n25.Pin_5, R3.Pin_1, U4.pin2
  N5: J1.pin1, R1.Pin_1, R4.Pin_1, Q1.drain
  N6: J1.pin2, J1.pin3, R5.Pin_1
  N7: J1.pin4, Q1.gate
  N8: R1.Pin_0, 400V_Bridge.pin6
  N9: R2.Pin_0, U4.pin3, R6.Pin_0
  N10: R2.Pin_1, U5.1
  N11: R3.Pin_0, U4.pin1
  N12: LED1.anode, R6.Pin_1
  N13: R4.Pin_0, U5.6
  N14: R5.Pin_0, 400V_Bridge.pin4
  N15: Q1.source, U5.4

notes:
  Load
  Mains
  MOC3021
  TIC206
  +
  -
  4N25
  Bridge
  G
  MT1
  MT2
  0-X
  In
  Gnd
  load
